// Logisim project 57114 NAND, NOR.circ as structural Verilog: 1 circuit, main circuit main
module main (
  input  in_1,
  input  in_2,
  input  in_3,
  input  in_4
);

  wire and_1_out, not_1_out, not_2_out, or_1_out;

  and and_1 (and_1_out, in_1, in_2);
  or or_1 (or_1_out, in_3, in_4);
  not not_1 (not_1_out, and_1_out);
  not not_2 (not_2_out, or_1_out);
  LED led_1 (.in(not_1_out));
  LED led_2 (.in(not_2_out));

  // Notes on the sheet:
  //   NAND GATE
  //   NOR GATE
endmodule
