// Logisim project Encoder.circ as structural Verilog: 1 circuit, main circuit main
module main (
  input  Y3,
  input  Y2,
  input  Y1,
  input  Y0
);

  wire and_1_out, not_1_out, or_1_out, or_2_out;

  not not_1 (not_1_out, Y2);
  or or_1 (or_1_out, Y3, Y2);
  and and_1 (and_1_out, not_1_out, Y1);
  LED A1 (.in(or_1_out));
  LED A0 (.in(or_2_out));
  or or_2 (or_2_out, and_1_out, Y3);

  // Notes on the sheet:
  //   2-Bit Encoder
endmodule
