// Logisim project MUX & DEMUX.circ as structural Verilog: 1 circuit, main circuit main
module main (
  input  A,
  input  S,
  input  B,
  input  C,
  input  INPUT
);

  wire and_1_out, and_2_out, and_3_out, and_4_out, not_1_out, not_2_out, or_1_out;

  not not_1 (not_1_out, S);
  not not_2 (not_2_out, C);
  and and_1 (and_1_out, A, not_1_out);
  and and_2 (and_2_out, S, B);
  or or_1 (or_1_out, and_1_out, and_2_out);
  and and_3 (and_3_out, not_2_out, INPUT);
  LED OUT_1 (.in(and_3_out));
  and and_4 (and_4_out, INPUT, C);
  LED OUT_2 (.in(and_4_out));
  LED led_1 (.in(or_1_out));

  // Notes on the sheet:
  //   2:1 Multiplexer
  //   1;2 DEMUX
endmodule
