// Logisim project Subtractors.circ as structural Verilog: 1 circuit, main circuit main
module main (
  input  A,
  input  B,
  input  A_2,
  input  B_2,
  input  C
);

  wire and_1_out, and_2_out, and_3_out, not_1_out, not_2_out, not_3_out, or_1_out, xor_1_out, xor_2_out,
       xor_3_out;

  xor xor_1 (xor_1_out, A, B);
  not not_1 (not_1_out, A);
  xor xor_2 (xor_2_out, B_2, C);
  not not_2 (not_2_out, B_2);
  LED Diff (.in(xor_1_out));
  and and_1 (and_1_out, B, not_1_out);
  xor xor_3 (xor_3_out, A_2, xor_2_out);
  not not_3 (not_3_out, xor_2_out);
  and and_2 (and_2_out, C, not_2_out);
  LED Borror (.in(and_1_out));
  LED Diff_2 (.in(xor_3_out));
  and and_3 (and_3_out, A_2, not_3_out);
  or or_1 (or_1_out, and_3_out, and_2_out);
  LED Borrow (.in(or_1_out));

  // Notes on the sheet:
  //   Half Subtractor
  //   Full Subtractor
endmodule
